// Logisim project s1.circ as structural Verilog
module Half_Adder (
  input  A,
  input  B,
  output Somma,
  output Riporto
);

  xor xor_1 (Somma, A, B);
  and and_1 (Riporto, A, B);
endmodule

module Full_Adder (
  input  A,
  input  B,
  input  C,
  output Somma,
  output Riporto
);

  wire and_1_out, and_2_out, and_3_out, xor_1_out;

  xor xor_1 (xor_1_out, A, B);
  and and_1 (and_1_out, A, C);
  and and_2 (and_2_out, A, B);
  and and_3 (and_3_out, B, C);
  xor xor_2 (Somma, xor_1_out, C);
  or or_1 (Riporto, and_1_out, and_2_out, and_3_out);
endmodule

module sommatore_8 (
  input  [7:0] A,
  input  [7:0] B,
  output [7:0] out_3,
  output overflow
);

  wire c1, c2, c3, c4, c5, c6, c7;

  Half_Adder half_adder_1 (.Somma(out_3[0]), .Riporto(c1), .A(A[0]), .B(B[0]));
  Full_Adder full_adder_1 (.Somma(out_3[7]), .Riporto(overflow), .A(A[7]), .B(B[7]), .C(c7));
  Full_Adder full_adder_2 (.Somma(out_3[6]), .Riporto(c7), .A(A[6]), .B(B[6]), .C(c6));
  Full_Adder full_adder_3 (.Somma(out_3[1]), .Riporto(c2), .A(A[1]), .B(B[1]), .C(c1));
  Full_Adder full_adder_4 (.Somma(out_3[2]), .Riporto(c3), .A(A[2]), .B(B[2]), .C(c2));
  Full_Adder full_adder_5 (.Somma(out_3[3]), .Riporto(c4), .A(A[3]), .B(B[3]), .C(c3));
  Full_Adder full_adder_6 (.Somma(out_3[4]), .Riporto(c5), .A(A[4]), .B(B[4]), .C(c4));
  Full_Adder full_adder_7 (.Somma(out_3[5]), .Riporto(c6), .A(A[5]), .B(B[5]), .C(c5));

  // Other names for the same wires on the sheet: a_t = A[1]; c = A[2]; e = A[3]; g = A[4]; i = A[5]; m = A[6];
  //   o = A[7]; b_t = B[1]; d = B[2]; f = B[3]; h = B[4]; l = B[5]; n = B[6]; p = B[7]; s1 = out_3[0]; s2 = out_3[1];
  //   s3 = out_3[2]; s4 = out_3[3]; s5 = out_3[4]; s6 = out_3[5]; s7 = out_3[6]; s8 = out_3[7]
endmodule

module sottrattore_8 (
  input  [7:0] A,
  input  [7:0] B,
  output [7:0] out_3,
  output overflow
);

  wire b_t, c1, c2, c3, c4, c5, c6, c7, d, f, h, l, n, p;
  wire [0:0] not_1_out;

  // Probe on A
  // Probe on B
  Full_Adder full_adder_1 (.Somma(out_3[0]), .Riporto(c1), .A(A[0]), .B(not_1_out[0]), .C(1'b1));
  Full_Adder full_adder_2 (.Somma(out_3[7]), .Riporto(overflow), .A(A[7]), .B(p), .C(c7));
  assign {p, n, l, h, f, d, b_t, not_1_out[0]} = ~B;  // NOT_Gate not_1, 8 bits wide
  Full_Adder full_adder_3 (.Somma(out_3[6]), .Riporto(c7), .A(A[6]), .B(n), .C(c6));
  Full_Adder full_adder_4 (.Somma(out_3[1]), .Riporto(c2), .A(A[1]), .B(b_t), .C(c1));
  Full_Adder full_adder_5 (.Somma(out_3[2]), .Riporto(c3), .A(A[2]), .B(d), .C(c2));
  Full_Adder full_adder_6 (.Somma(out_3[3]), .Riporto(c4), .A(A[3]), .B(f), .C(c3));
  Full_Adder full_adder_7 (.Somma(out_3[4]), .Riporto(c5), .A(A[4]), .B(h), .C(c4));
  Full_Adder full_adder_8 (.Somma(out_3[5]), .Riporto(c6), .A(A[5]), .B(l), .C(c5));
  // Probe on out_3

  // Other names for the same wires on the sheet: a_t = A[1]; c = A[2]; e = A[3]; g = A[4]; i = A[5]; m = A[6];
  //   o = A[7]; s1 = out_3[0]; s2 = out_3[1]; s3 = out_3[2]; s4 = out_3[3]; s5 = out_3[4]; s6 = out_3[5];
  //   s7 = out_3[6]; s8 = out_3[7]
endmodule

module AiArith (
  input  in_1,
  input  [7:0] in_2,
  input  [7:0] in_3
);

  sottrattore_8 sottrattore_8_1 (.A(in_2), .B(in_3));  // open: out_3, overflow
endmodule

module AND_8bit (
  input  [7:0] in_1,
  input  [7:0] in_2,
  output [7:0] out_3
);

  assign out_3 = in_1 & in_2;  // AND_Gate and_1, 8 bits wide
endmodule

module OR_8bit (
  input  [7:0] in_1,
  input  [7:0] in_2,
  output [7:0] out_3
);

  assign out_3 = in_1 | in_2;  // OR_Gate or_1, 8 bits wide
endmodule

module NOT_8bit (
  input  [7:0] in_1,
  output [7:0] out_2
);

  assign out_2 = ~in_1;  // NOT_Gate not_1, 8 bits wide
endmodule

module EX_OR_8bit (
  input  [7:0] in_1,
  input  [7:0] in_2,
  output [7:0] out_3
);

  assign out_3 = in_1 ^ in_2;  // XOR_Gate xor_1, 8 bits wide
endmodule
